// Logisim project CyProcessingUnit.circ as structural Verilog: 2 circuits, main circuit main
module main (
  input  [23:0] in_1,
  output [7:0] Data,
  output [7:0] A,
  output [7:0] B,
  output [7:0] C
);

  wire alu_1_error, registerband_8bit_1_s_1bit;
  wire [3:0] decoder_24bits_1_operation, decoder_24bits_1_rin1, decoder_24bits_1_rin2, decoder_24bits_1_rout,
       decoder_24bits_1_type_op, decoder_operation_1_s;

  Decoder_24bits decoder_24bits_1 (
    .Bits24(in_1), .WE(1'b1), .zero(registerband_8bit_1_s_1bit), .Rout(decoder_24bits_1_rout),
    .Rin2(decoder_24bits_1_rin2), .Rin1(decoder_24bits_1_rin1), .Operation(decoder_24bits_1_operation),
    .Type_Op(decoder_24bits_1_type_op));  // open: Unused
  RegisterBand_8bit registerband_8bit_1 (
    .Data(C), .SlctA(decoder_24bits_1_rin1[2:0]), .SlctC(decoder_24bits_1_rout),
    .SlctB(decoder_24bits_1_rin2[2:0]), .A(A), .B(B), .S_1bit(registerband_8bit_1_s_1bit));
  Decoder_Operation decoder_operation_1 (
    .A({decoder_24bits_1_type_op, decoder_24bits_1_operation}), .S(decoder_operation_1_s));
  LED led_1 (.in(alu_1_error));
  ALU alu_1 (.A(A), .B(B), .SlctOP(decoder_operation_1_s), .Error(alu_1_error), .C(C));

  assign Data = C;
endmodule

module Decoder_Operation (
  input  [7:0] A,
  output [3:0] S
);

  wire not_2_out, not_3_out, or_1_out, or_2_out, or_3_out, or_4_out, or_5_out, or_6_out;

  not not_1 (S[2], A[4]);
  not not_2 (not_2_out, A[3]);
  not not_3 (not_3_out, A[1]);
  or or_1 (or_1_out, A[4], A[3]);
  or or_2 (or_2_out, S[2], not_2_out);
  or or_3 (or_3_out, S[2], A[1]);
  or or_4 (or_4_out, A[4], not_3_out);
  or or_5 (or_5_out, A[4], A[2]);
  or or_6 (or_6_out, A[2], A[0]);
  and and_1 (S[3], or_1_out, or_2_out);
  and and_2 (S[1], not_2_out, or_3_out, or_4_out);
  and and_3 (S[0], or_5_out, or_6_out);
endmodule
